// Logisim project logisim.circ as structural Verilog: 1 circuit, main circuit main
module main (
  input  in_1,
  input  in_2,
  input  in_3,
  input  in_4,
  input  in_5,
  input  in_6,
  input  in_7,
  input  [7:0] in_8,
  input  [7:0] in_9
);

  wire nand_1_out, nand_2_out, nand_3_out, nand_4_out, nand_5_out, nand_6_out, nand_7_out, nand_10_out,
       nand_11_out, nand_12_out, nand_13_out, nand_14_out, nand_15_out, nand_16_out, nand_17_out, or_1_out;

  // Probe on nand_1_out
  nand nand_1 (nand_1_out, in_1, in_1);
  nand nand_2 (nand_2_out, in_2, in_3);
  nand nand_3 (nand_3_out, in_4, in_4);
  nand nand_4 (nand_4_out, in_5, in_5);
  nand nand_5 (nand_5_out, in_6, in_7);
  or or_1 (or_1_out, in_6, in_7);
  nand nand_6 (nand_6_out, nand_2_out, nand_2_out);
  nand nand_7 (nand_7_out, nand_3_out, nand_4_out);
  nand nand_8 (in_8[0], in_9[0], in_9[0]);
  nand nand_9 (in_8[1], in_9[1], in_9[1]);
  nand nand_10 (nand_10_out, in_9[2], in_9[2]);
  nand nand_11 (nand_11_out, in_9[3], in_9[3]);
  nand nand_12 (nand_12_out, in_9[4], in_9[4]);
  nand nand_13 (nand_13_out, in_9[5], in_9[5]);
  nand nand_14 (nand_14_out, in_9[6], in_9[6]);
  nand nand_15 (nand_15_out, in_9[7], in_9[7]);
  // Probe on nand_6_out
  // Probe on nand_7_out
  nand nand_16 (nand_16_out, nand_5_out, or_1_out);
  // Probe on nand_17_out
  nand nand_17 (nand_17_out, nand_16_out, nand_16_out);
  // Pins of 2 and 8 bits meet at in_8
endmodule
